# Fritzing sketch FKODI_fan (saved by Fritzing 0.9.3b)

parts:
  Q1 = NPN-Transistor [package="TO92 [THT]"]
  F1 = Fan - Ventilador [package=THT]
  Raspberry_Pi_1 = Raspberry Pi 3 [part_number=RPI-3-V1.2]

nets:
  N1: Q1.E, Raspberry_Pi_1.GND
  N2: Q1.B, Raspberry_Pi_1.GIPO24
  N3: Q1.C, F1.GND
  5V: F1.5V, Raspberry_Pi_1.5V

custom parts:
  Fan - Ventilador: Ventilador de 2 pines, se encuentra comunmente en computadoras de escritorio
